// Logisim project Lab1.circ as structural Verilog: 12 circuits, main circuit main
module main (
  input  ReadEnable,
  input  Reset,
  input  [6:0] in_3,
  input  [6:0] in_4,
  input  [6:0] in_5,
  input  [6:0] in_6,
  input  [6:0] in_7,
  output [6:0] Char
);

  wire CLK_out, decoascii_7segm_1_a, decoascii_7segm_1_b, decoascii_7segm_1_c, decoascii_7segm_1_d,
       decoascii_7segm_1_e, decoascii_7segm_1_f, decoascii_7segm_1_g, keyboard_1_avail;

  Clock CLK (.out(CLK_out));
  Keyboard keyboard_1 (.clk(CLK_out), .re(ReadEnable), .clr(Reset), .avail(keyboard_1_avail), .data(Char));
  DotMatrix dotmatrix_1 (.col0(in_3), .col1(in_4), .col2(in_5), .col3(in_6), .col4(in_7));
  LED Available (.in(keyboard_1_avail));
  DecoAscii_7segm decoascii_7segm_1 (
    .ascii(Char), .a(decoascii_7segm_1_a), .b(decoascii_7segm_1_b), .c(decoascii_7segm_1_c),
    .d(decoascii_7segm_1_d), .e(decoascii_7segm_1_e), .f(decoascii_7segm_1_f), .g(decoascii_7segm_1_g));
  _7_Segment_Display u_7_segment_display_1 (
    .g(decoascii_7segm_1_g), .f(decoascii_7segm_1_f), .a(decoascii_7segm_1_a), .b(decoascii_7segm_1_b),
    .e(decoascii_7segm_1_e), .d(decoascii_7segm_1_d), .c(decoascii_7segm_1_c));  // open: dp
endmodule

module DecoAscii_7segm (
  input  [6:0] ascii,
  output a,
  output b,
  output c,
  output d,
  output e,
  output f,
  output g
);

  wire and_1_out, and_2_out, and_3_out, and_4_out, and_5_out, and_6_out, and_7_out, and_8_out, and_9_out,
       and_10_out, and_11_out, and_12_out, and_13_out, and_14_out, and_15_out, and_16_out, and_17_out,
       and_18_out, and_19_out, and_20_out, and_21_out, and_22_out, and_23_out, and_24_out, and_25_out,
       and_26_out, not_1_out, not_2_out, not_3_out, not_4_out, not_5_out;

  not not_1 (not_1_out, ascii[6]);
  not not_2 (not_2_out, ascii[3]);
  not not_3 (not_3_out, ascii[2]);
  not not_4 (not_4_out, ascii[1]);
  not not_5 (not_5_out, ascii[0]);
  and and_1 (and_1_out, not_1_out, ascii[5], ascii[4], not_2_out, ascii[1]);
  and and_2 (and_2_out, not_1_out, ascii[5], ascii[4], not_2_out, ascii[2], ascii[0]);
  and and_3 (and_3_out, not_1_out, ascii[5], ascii[4], ascii[3], not_3_out, not_4_out);
  and and_4 (and_4_out, not_1_out, ascii[5], ascii[4], not_2_out, not_3_out, not_5_out);
  and and_5 (and_5_out, not_1_out, ascii[5], ascii[4], not_2_out, not_3_out);
  and and_6 (and_6_out, not_1_out, ascii[5], ascii[4], not_2_out, not_4_out, not_5_out);
  and and_7 (and_7_out, not_1_out, ascii[5], ascii[4], not_2_out, ascii[1], ascii[0]);
  and and_8 (and_8_out, not_1_out, ascii[5], ascii[4], not_3_out, not_4_out);
  and and_9 (and_9_out, not_1_out, ascii[5], ascii[4], not_2_out, ascii[0]);
  and and_10 (and_10_out, not_1_out, ascii[5], ascii[4], not_2_out, ascii[2]);
  and and_11 (and_11_out, not_1_out, ascii[5], ascii[4], not_3_out, not_4_out);
  and and_12 (and_12_out, not_1_out, ascii[5], ascii[4], not_2_out, not_3_out, ascii[1]);
  and and_13 (and_13_out, not_1_out, ascii[5], ascii[4], not_2_out, ascii[2], not_4_out, ascii[0]);
  and and_14 (and_14_out, not_1_out, ascii[5], ascii[4], not_2_out, ascii[1], not_5_out);
  and and_15 (and_15_out, not_1_out, ascii[5], ascii[4], ascii[3], not_3_out, not_4_out);
  and and_16 (and_16_out, not_1_out, ascii[5], ascii[4], not_2_out, not_3_out, not_5_out);
  and and_17 (and_17_out, not_1_out, ascii[5], ascii[4], not_2_out, ascii[1], not_5_out);
  and and_18 (and_18_out, not_1_out, ascii[5], ascii[4], not_3_out, not_4_out, not_5_out);
  and and_19 (and_19_out, not_1_out, ascii[5], ascii[4], not_2_out, ascii[2], not_4_out);
  and and_20 (and_20_out, not_1_out, ascii[5], ascii[4], not_2_out, ascii[2], not_5_out);
  and and_21 (and_21_out, not_1_out, ascii[5], ascii[4], ascii[3], not_3_out, not_4_out);
  and and_22 (and_22_out, not_1_out, ascii[5], ascii[4], not_2_out, not_4_out, not_5_out);
  and and_23 (and_23_out, not_1_out, ascii[5], ascii[4], not_2_out, not_3_out, ascii[1]);
  and and_24 (and_24_out, not_1_out, ascii[5], ascii[4], not_2_out, ascii[2], not_4_out);
  and and_25 (and_25_out, not_1_out, ascii[5], ascii[4], ascii[3], not_3_out, not_4_out);
  and and_26 (and_26_out, not_1_out, ascii[5], ascii[4], not_2_out, ascii[1], not_5_out);
  or or_1 (a, and_1_out, and_2_out, and_3_out, and_4_out);
  or or_2 (b, and_5_out, and_6_out, and_7_out, and_8_out);
  or or_3 (c, and_9_out, and_10_out, and_11_out);
  or or_4 (d, and_12_out, and_13_out, and_14_out, and_15_out, and_16_out);
  or or_5 (e, and_17_out, and_18_out);
  or or_6 (f, and_19_out, and_20_out, and_21_out, and_22_out);
  or or_7 (g, and_23_out, and_24_out, and_25_out, and_26_out);
endmodule

module pruebaram (
  input  [6:0] in_1,
  input  in_2,
  input  in_3,
  input  ESCRIBIR,
  input  LEER,
  input  ReadEnable,
  input  in_7,
  input  Reset,
  output [6:0] out_9
);

  wire clock_1_out, clock_2_out, clock_3_out, contadora5_1_z, keyboard_1_avail, multiplexer_1_out, not_1_out,
       not_2_out, resetcomp_1_shouldreset;
  wire [2:0] contadora5_1_out_4;
  wire [6:0] adder_1_out, keyboard_1_data, multiplier_1_out, otrocondatodr_1_out_3, rom_1_data,
       subtractor_1_out;

  Clock #(.highDuration(7), .lowDuration(7)) clock_1 (.out(clock_1_out));
  Clock clock_2 (.out(clock_2_out));
  Keyboard keyboard_1 (
    .clk(clock_2_out), .re(ReadEnable), .clr(Reset), .avail(keyboard_1_avail), .data(keyboard_1_data));
  ResetComp resetcomp_1 (
    .AVAILABLE(keyboard_1_avail), .CLK(multiplexer_1_out), .REESET(in_2),
    .ShouldReset(resetcomp_1_shouldreset));
  not not_1 (not_1_out, clock_1_out);
  Clock clock_3 (.out(clock_3_out));
  Multiplexer multiplexer_1 (.in0(contadora5_1_z), .in1(clock_3_out), .out(multiplexer_1_out), .sel(keyboard_1_avail));
  otrocondatodr otrocondatodr_1 (.RESET(in_3), .CLK(multiplexer_1_out), .out_3(otrocondatodr_1_out_3));
  RAM #(.addrWidth(7), .dataWidth(7)) ram_1 (
    .addr(otrocondatodr_1_out_3), .we(ESCRIBIR), .oe(LEER), .clk(multiplexer_1_out), .din(keyboard_1_data),
    .dout(out_9));
  LED Available (.in(keyboard_1_avail));
  not not_2 (not_2_out, keyboard_1_avail);
  Subtractor #(.width(7)) subtractor_1 (.a(out_9), .b(7'b0100000), .out(subtractor_1_out));  // open: bin, bout
  Multiplier #(.width(7)) multiplier_1 (
    .a(subtractor_1_out), .b(7'b0000110), .out(multiplier_1_out));  // open: cin, cout
  ContadorA5 contadora5_1 (
    .CLK(clock_3_out), .X(not_2_out), .RESET(in_3), .out_4(contadora5_1_out_4), .Z(contadora5_1_z));
  Adder #(.width(7)) adder_1 (
    .a(multiplier_1_out), .b({4'b0000, contadora5_1_out_4}), .out(adder_1_out));  // open: cin, cout
  ROM #(.addrWidth(10), .dataWidth(7)) rom_1 (.addr({3'b000, adder_1_out}), .data(rom_1_data));
  pantalla pantalla_1 (.DIN(rom_1_data), .RESET(in_7));
endmodule

module contador (
  input  Cnt,
  output [1:0] out_2
);

  wire and_1_out, and_2_out, and_3_out, CLK, FF0_qn, FF1_qn, not_1_out, or_1_out, xor_1_out;

  Clock u_CLK (.out(CLK));
  not not_1 (not_1_out, Cnt);
  and and_1 (and_1_out, not_1_out, out_2[1]);
  and and_2 (and_2_out, out_2[0], Cnt, FF1_qn);
  and and_3 (and_3_out, Cnt, out_2[1], FF0_qn);
  xor xor_1 (xor_1_out, out_2[0], Cnt);
  or or_1 (or_1_out, and_1_out, and_2_out, and_3_out);
  D_Flip_Flop FF0 (.D(xor_1_out), .clk(CLK), .Q(out_2[0]), .Qn(FF0_qn));  // open: preset, reset
  D_Flip_Flop FF1 (.D(or_1_out), .clk(CLK), .Q(out_2[1]), .Qn(FF1_qn));  // open: preset, reset

  // Other names for the same wires on the sheet: S0 = out_2[0]; S1 = out_2[1]
endmodule

module contador7 (
  input  C,
  input  R,
  output out_3
);

  wire s_r_ff_1_q, s_r_ff_1_qn, s_r_ff_2_q, s_r_ff_2_qn, s_r_ff_3_q, s_r_ff_3_qn;

  S_R_Flip_Flop s_r_ff_1 (
    .S(s_r_ff_1_qn), .R(s_r_ff_1_q), .clk(C), .Q(s_r_ff_1_q), .Qn(s_r_ff_1_qn));  // open: reset, preset
  S_R_Flip_Flop s_r_ff_2 (
    .S(s_r_ff_2_qn), .R(s_r_ff_2_q), .clk(s_r_ff_1_qn), .Q(s_r_ff_2_q), .Qn(s_r_ff_2_qn));  // open: reset, preset
  S_R_Flip_Flop s_r_ff_3 (
    .S(s_r_ff_3_qn), .R(s_r_ff_3_q), .clk(s_r_ff_2_qn), .Q(s_r_ff_3_q), .reset(R), .Qn(s_r_ff_3_qn));  // open: preset
  and and_1 (out_3, s_r_ff_3_q, s_r_ff_2_q, s_r_ff_1_q);
endmodule

module INSERTARDATO (
  input  [6:0] in_1
);

  D_Flip_Flop d_ff_1 (.D(in_1[0]));  // open: clk, Q, Qn, preset, reset
  // Pins of 1 and 7 bits meet at in_1
endmodule

module otrocondatodr (
  input  RESET,
  input  CLK,
  output [6:0] out_3
);

  Counter #(.max('h7f), .width(7)) counter_1 (.clr(RESET), .clk(CLK), .Q(out_3));  // open: load, up, count, D, carry
endmodule

module ResetComp (
  input  AVAILABLE,
  input  CLK,
  input  REESET,
  output ShouldReset
);

  wire d_ff_1_q, d_ff_1_qn, not_1_out, or_1_out, t_ff_1_q;

  not not_1 (not_1_out, AVAILABLE);
  or or_1 (or_1_out, t_ff_1_q, not_1_out);
  T_Flip_Flop t_ff_1 (.T(or_1_out), .clk(CLK), .Q(t_ff_1_q), .reset(REESET));  // open: Qn, preset
  D_Flip_Flop d_ff_1 (.D(t_ff_1_q), .clk(CLK), .Q(d_ff_1_q), .Qn(d_ff_1_qn), .preset(d_ff_1_q), .reset(REESET));
  and and_1 (ShouldReset, t_ff_1_q, d_ff_1_qn);
endmodule

module ContadorA5 (
  input  CLK,
  input  X,
  input  RESET,
  output [2:0] out_4,
  output Z
);

  wire and_1_out, and_2_out, and_3_out, and_4_out, and_5_out, NotQ0, NotQ1, NotQ2, or_1_out;

  and and_1 (and_1_out, X, NotQ1);
  and and_2 (and_2_out, X, NotQ2);
  and and_3 (and_3_out, out_4[0], X, NotQ2);
  and and_4 (and_4_out, X, out_4[0], out_4[1], NotQ2);
  and and_5 (and_5_out, X, out_4[0], NotQ1);
  or or_1 (or_1_out, and_1_out, and_2_out);
  J_K_Flip_Flop j_k_ff_1 (
    .J(or_1_out), .K(or_1_out), .clk(CLK), .Q(out_4[0]), .Qn(NotQ0), .reset(RESET));  // open: preset
  J_K_Flip_Flop j_k_ff_2 (
    .J(and_3_out), .K(and_3_out), .clk(CLK), .Q(out_4[1]), .Qn(NotQ1), .reset(RESET));  // open: preset
  J_K_Flip_Flop j_k_ff_3 (
    .J(and_4_out), .K(and_5_out), .clk(CLK), .Q(out_4[2]), .Qn(NotQ2), .reset(RESET));  // open: preset
  Comparator #(.width(3)) comparator_1 (.a(out_4), .b(3'b101), .eq(Z));  // open: gt, lt

  // Other names for the same wires on the sheet: Q0 = out_4[0]; Q1 = out_4[1]; Q2 = out_4[2]

  // Notes on the sheet:
  //   SALIDA Q0
  //   SALIDA Q1
  //   SALIDA Q2
endmodule

module ten_registers (
  input  [6:0] DIN,
  input  CLK,
  input  RESET,
  output [6:0] DO1,
  output [6:0] DO2,
  output [6:0] DO3,
  output [6:0] DO4,
  output [6:0] DO5,
  output [6:0] DO6,
  output [6:0] DO7,
  output [6:0] DO8,
  output [6:0] DO9,
  output [6:0] DO10
);

  Register #(.width(7)) register_1 (.D(DIN), .clk(CLK), .Q(DO1), .clr(RESET));  // open: en
  Register #(.width(7)) register_2 (.D(DO1), .clk(CLK), .Q(DO2), .clr(RESET));  // open: en
  Register #(.width(7)) register_3 (.D(DO2), .clk(CLK), .Q(DO3), .clr(RESET));  // open: en
  Register #(.width(7)) register_4 (.D(DO3), .clk(CLK), .Q(DO4), .clr(RESET));  // open: en
  Register #(.width(7)) register_5 (.D(DO4), .clk(CLK), .Q(DO5), .clr(RESET));  // open: en
  Register #(.width(7)) register_6 (.D(DO5), .clk(CLK), .Q(DO6), .clr(RESET));  // open: en
  Register #(.width(7)) register_7 (.D(DO6), .clk(CLK), .Q(DO7), .clr(RESET));  // open: en
  Register #(.width(7)) register_8 (.D(DO7), .clk(CLK), .Q(DO8), .clr(RESET));  // open: en
  Register #(.width(7)) register_9 (.D(DO8), .clk(CLK), .Q(DO9), .clr(RESET));  // open: en
  Register #(.width(7)) register_10 (.D(DO9), .clk(CLK), .Q(DO10), .clr(RESET));  // open: en
endmodule

module pantalla (
  input  [6:0] DIN,
  input  RESET
);

  wire clock_1_out;
  wire [6:0] ten_registers_1_do1, ten_registers_1_do2, ten_registers_1_do3, ten_registers_1_do4,
       ten_registers_1_do5, ten_registers_1_do6, ten_registers_1_do7, ten_registers_1_do8,
       ten_registers_1_do9, ten_registers_1_do10, ten_registers_2_do1, ten_registers_2_do2,
       ten_registers_2_do3, ten_registers_2_do4, ten_registers_2_do5, ten_registers_2_do6,
       ten_registers_2_do7, ten_registers_2_do8, ten_registers_2_do9, ten_registers_2_do10,
       ten_registers_3_do1, ten_registers_3_do2, ten_registers_3_do3, ten_registers_3_do4,
       ten_registers_3_do5, ten_registers_3_do6, ten_registers_3_do7, ten_registers_3_do8,
       ten_registers_3_do9, ten_registers_3_do10, ten_registers_4_do1, ten_registers_4_do2,
       ten_registers_4_do3, ten_registers_4_do4, ten_registers_4_do5, ten_registers_4_do6,
       ten_registers_4_do7, ten_registers_4_do8, ten_registers_4_do9, ten_registers_4_do10,
       ten_registers_5_do1, ten_registers_5_do2, ten_registers_5_do3, ten_registers_5_do4,
       ten_registers_5_do5, ten_registers_5_do6, ten_registers_5_do7, ten_registers_5_do8,
       ten_registers_5_do9, ten_registers_5_do10, ten_registers_6_do1, ten_registers_6_do2,
       ten_registers_6_do3, ten_registers_6_do4, ten_registers_6_do5, ten_registers_6_do6,
       ten_registers_6_do7, ten_registers_6_do8, ten_registers_6_do9, ten_registers_6_do10;

  Clock clock_1 (.out(clock_1_out));
  DotMatrix #(.matrixcols(60)) dotmatrix_1 (
    .col0(ten_registers_6_do10), .col1(ten_registers_6_do9), .col2(ten_registers_6_do8),
    .col3(ten_registers_6_do7), .col4(ten_registers_6_do6), .col5(ten_registers_6_do5),
    .col6(ten_registers_6_do4), .col7(ten_registers_6_do3), .col8(ten_registers_6_do2),
    .col9(ten_registers_6_do1), .col10(ten_registers_5_do10), .col11(ten_registers_5_do9),
    .col12(ten_registers_5_do8), .col13(ten_registers_5_do7), .col14(ten_registers_5_do6),
    .col15(ten_registers_5_do5), .col16(ten_registers_5_do4), .col17(ten_registers_5_do3),
    .col18(ten_registers_5_do2), .col19(ten_registers_5_do1), .col20(ten_registers_4_do10),
    .col21(ten_registers_4_do9), .col22(ten_registers_4_do8), .col23(ten_registers_4_do7),
    .col24(ten_registers_4_do6), .col25(ten_registers_4_do5), .col26(ten_registers_4_do4),
    .col27(ten_registers_4_do3), .col28(ten_registers_4_do2), .col29(ten_registers_4_do1),
    .col30(ten_registers_3_do10), .col31(ten_registers_3_do9), .col32(ten_registers_3_do8),
    .col33(ten_registers_3_do7), .col34(ten_registers_3_do6), .col35(ten_registers_3_do5),
    .col36(ten_registers_3_do4), .col37(ten_registers_3_do3), .col38(ten_registers_3_do2),
    .col39(ten_registers_3_do1), .col40(ten_registers_2_do10), .col41(ten_registers_2_do9),
    .col42(ten_registers_2_do8), .col43(ten_registers_2_do7), .col44(ten_registers_2_do6),
    .col45(ten_registers_2_do5), .col46(ten_registers_2_do4), .col47(ten_registers_2_do3),
    .col48(ten_registers_2_do2), .col49(ten_registers_2_do1), .col50(ten_registers_1_do10),
    .col51(ten_registers_1_do9), .col52(ten_registers_1_do8), .col53(ten_registers_1_do7),
    .col54(ten_registers_1_do6), .col55(ten_registers_1_do5), .col56(ten_registers_1_do4),
    .col57(ten_registers_1_do3), .col58(ten_registers_1_do2), .col59(ten_registers_1_do1));
  ten_registers ten_registers_1 (
    .DIN(DIN), .CLK(clock_1_out), .RESET(RESET), .DO1(ten_registers_1_do1), .DO2(ten_registers_1_do2),
    .DO3(ten_registers_1_do3), .DO4(ten_registers_1_do4), .DO5(ten_registers_1_do5),
    .DO6(ten_registers_1_do6), .DO7(ten_registers_1_do7), .DO8(ten_registers_1_do8),
    .DO9(ten_registers_1_do9), .DO10(ten_registers_1_do10));
  ten_registers ten_registers_2 (
    .DIN(ten_registers_1_do10), .CLK(clock_1_out), .RESET(RESET), .DO1(ten_registers_2_do1),
    .DO2(ten_registers_2_do2), .DO3(ten_registers_2_do3), .DO4(ten_registers_2_do4),
    .DO5(ten_registers_2_do5), .DO6(ten_registers_2_do6), .DO7(ten_registers_2_do7),
    .DO8(ten_registers_2_do8), .DO9(ten_registers_2_do9), .DO10(ten_registers_2_do10));
  ten_registers ten_registers_3 (
    .DIN(ten_registers_2_do10), .CLK(clock_1_out), .RESET(RESET), .DO1(ten_registers_3_do1),
    .DO2(ten_registers_3_do2), .DO3(ten_registers_3_do3), .DO4(ten_registers_3_do4),
    .DO5(ten_registers_3_do5), .DO6(ten_registers_3_do6), .DO7(ten_registers_3_do7),
    .DO8(ten_registers_3_do8), .DO9(ten_registers_3_do9), .DO10(ten_registers_3_do10));
  ten_registers ten_registers_4 (
    .DIN(ten_registers_3_do10), .CLK(clock_1_out), .RESET(RESET), .DO1(ten_registers_4_do1),
    .DO2(ten_registers_4_do2), .DO3(ten_registers_4_do3), .DO4(ten_registers_4_do4),
    .DO5(ten_registers_4_do5), .DO6(ten_registers_4_do6), .DO7(ten_registers_4_do7),
    .DO8(ten_registers_4_do8), .DO9(ten_registers_4_do9), .DO10(ten_registers_4_do10));
  ten_registers ten_registers_5 (
    .DIN(ten_registers_4_do10), .CLK(clock_1_out), .RESET(RESET), .DO1(ten_registers_5_do1),
    .DO2(ten_registers_5_do2), .DO3(ten_registers_5_do3), .DO4(ten_registers_5_do4),
    .DO5(ten_registers_5_do5), .DO6(ten_registers_5_do6), .DO7(ten_registers_5_do7),
    .DO8(ten_registers_5_do8), .DO9(ten_registers_5_do9), .DO10(ten_registers_5_do10));
  ten_registers ten_registers_6 (
    .DIN(ten_registers_5_do10), .CLK(clock_1_out), .RESET(RESET), .DO1(ten_registers_6_do1),
    .DO2(ten_registers_6_do2), .DO3(ten_registers_6_do3), .DO4(ten_registers_6_do4),
    .DO5(ten_registers_6_do5), .DO6(ten_registers_6_do6), .DO7(ten_registers_6_do7),
    .DO8(ten_registers_6_do8), .DO9(ten_registers_6_do9), .DO10(ten_registers_6_do10));
endmodule

module ContadorA6 (
  input  CLK,
  input  X,
  input  RESET,
  output [2:0] out_4,
  output Z
);

  wire and_1_out, and_2_out, and_3_out, and_4_out, and_5_out, and_6_out, and_7_out, NotQ0, NotQ1, NotQ2,
       or_1_out, or_2_out;

  and and_1 (and_1_out, NotQ1, X);
  and and_2 (and_2_out, NotQ2, X);
  and and_3 (and_3_out, X, out_4[2]);
  and and_4 (and_4_out, NotQ2, out_4[0], X);
  and and_5 (and_5_out, NotQ1, out_4[0], X);
  and and_6 (and_6_out, X, out_4[0], out_4[1], NotQ2);
  and and_7 (and_7_out, X, out_4[1], NotQ0);
  or or_1 (or_1_out, and_1_out, and_2_out);
  or or_2 (or_2_out, and_3_out, and_4_out);
  J_K_Flip_Flop j_k_ff_1 (
    .J(or_1_out), .K(or_1_out), .clk(CLK), .Q(out_4[0]), .Qn(NotQ0), .reset(RESET));  // open: preset
  J_K_Flip_Flop j_k_ff_2 (
    .J(and_5_out), .K(or_2_out), .clk(CLK), .Q(out_4[1]), .Qn(NotQ1), .reset(RESET));  // open: preset
  J_K_Flip_Flop j_k_ff_3 (
    .J(and_6_out), .K(and_7_out), .clk(CLK), .Q(out_4[2]), .Qn(NotQ2), .reset(RESET));  // open: preset
  Comparator #(.width(3)) comparator_1 (.a(out_4), .b(3'b110), .eq(Z));  // open: gt, lt

  // Other names for the same wires on the sheet: Q0 = out_4[0]; Q1 = out_4[1]; Q2 = out_4[2]

  // Notes on the sheet:
  //   SALIDA Q1
  //   SALIDA Q2
endmodule
